// Logisim project rewrited_regfile.circ as structural Verilog: 1 circuit, main circuit main
module main (
  input  [4:0] rs1,
  input  [4:0] rs2,
  input  [4:0] rd,
  input  [31:0] Write_Data,
  input  RegWEn,
  input  clk,
  output [31:0] ra,
  output [31:0] sp,
  output [31:0] t0,
  output [31:0] t1,
  output [31:0] t2,
  output [31:0] s0,
  output [31:0] s1,
  output [31:0] a0,
  output [31:0] Read_Data_1,
  output [31:0] Read_Data_2
);

  wire [31:0] demultiplexer_1_out1, demultiplexer_2_out1, demultiplexer_2_out2, demultiplexer_2_out5,
       demultiplexer_2_out6, demultiplexer_2_out7, demultiplexer_2_out8, demultiplexer_2_out9,
       demultiplexer_2_out10;

  Multiplexer #(.select(5), .width(32), .enable("false")) multiplexer_1 (
    .in0({32{1'b0}}), .in1(ra), .in2(sp), .in5(t0), .in6(t1), .in7(t2), .in8(s0), .in9(s1), .in10(a0),
    .out(Read_Data_1), .sel(rs1));  // open: in3, in4, in11, in12, in13, in14, in15, in16, in17, in18, in19, in20, in21, in22, in23, in24, in25, in26, in27, in28, in29, in30, in31
  Demultiplexer #(.width(32), .enable("false")) demultiplexer_1 (
    .out1(demultiplexer_1_out1), .in(Write_Data), .sel(RegWEn));  // open: out0
  Demultiplexer #(.select(5), .width(32), .enable("false")) demultiplexer_2 (
    .out1(demultiplexer_2_out1), .out2(demultiplexer_2_out2), .out5(demultiplexer_2_out5),
    .out6(demultiplexer_2_out6), .out7(demultiplexer_2_out7), .out8(demultiplexer_2_out8),
    .out9(demultiplexer_2_out9), .out10(demultiplexer_2_out10), .in(demultiplexer_1_out1));  // open: out0, out3, out4, out11, out12, out13, out14, out15, out16, out17, out18, out19, out20, out21, out22, out23, out24, out25, out26, out27, out28, out29, out30, out31, sel
  Register #(.width(32)) register_1 (.D(demultiplexer_2_out9), .clk(clk), .Q(s1));  // open: en, clr
  Register #(.width(32)) register_2 (.D(demultiplexer_2_out10), .clk(clk), .Q(a0));  // open: en, clr
  Multiplexer #(.select(5), .width(32), .enable("false")) multiplexer_2 (
    .in0({32{1'b0}}), .in1(ra), .in2(sp), .in5(t0), .in6(t1), .in7(t2), .in8(s0), .in9(s1), .in10(a0),
    .out(Read_Data_2), .sel(rs2));  // open: in3, in4, in11, in12, in13, in14, in15, in16, in17, in18, in19, in20, in21, in22, in23, in24, in25, in26, in27, in28, in29, in30, in31
  Register #(.width(32)) register_3 (.D(demultiplexer_2_out6), .clk(clk), .Q(t1));  // open: en, clr
  Register #(.width(32)) register_4 (.D(demultiplexer_2_out7), .clk(clk), .Q(t2));  // open: en, clr
  Register #(.width(32)) register_5 (.D(demultiplexer_2_out8), .clk(clk), .Q(s0));  // open: en, clr
  Register #(.width(32)) register_6 (.D(demultiplexer_2_out2), .clk(clk), .Q(sp));  // open: en, clr
  Register #(.width(32)) register_7 (.D(demultiplexer_2_out5), .clk(clk), .Q(t0));  // open: en, clr
  Register #(.width(32)) register_8 (.D(demultiplexer_2_out1), .clk(clk), .Q(ra));  // open: en, clr

  // Other names for the same wires on the sheet: read_data1[31:0] = Read_Data_1; read_data2[31:0] = Read_Data_2;
  //   read_reg1[4:0] = rs1; read_reg2[4:0] = rs2; write_en = RegWEn; write_reg[4:0] = rd

  // Notes on the sheet:
  //   INPUTS to your circuit
  //   DON'T CHANGE THE LOCATIONS OF THE INPUTS AND OUTPUTS!
  //   These are DEBUG/TEST outputs from your circuit.
  //   OUTPUTS from your circuit
endmodule
