// Logisim project alu.circ as structural Verilog: 1 circuit, main circuit alu
module alu (
  input  [31:0] A,
  input  [31:0] B,
  input  [3:0] ALUSel,
  output [31:0] Result
);

  wire comparator_1_lt, comparator_2_gt, comparator_3_gt, comparator_4_eq, sgn;
  wire [4:0] bit_extender_2_out, bit_extender_3_out, bit_extender_4_out;
  wire [5:0] adder_1_out, bitadder_1_out, bitadder_2_out;
  wire [31:0] abs_A, abs_B, abs_sh, abs_sl, add, adder_3_out, and1, cnto13, divu8, mulh14, mulhu11, mult10,
       multiplexer_5_out, neg_A, neg_B, negator_2_out, not_1_out, or2, remu9, shifter_4_out, shifter_5_out,
       sll6, slt7, sra5, srl4, sub12, undriven, xor3, xor_2_out;

  Subtractor #(.width(32)) subtractor_1 (.a(A), .b(B), .out(sub12));  // open: bin, bout
  BitAdder #(.width(32)) bitadder_1 (.in0(A), .out(bitadder_1_out));
  BitAdder #(.width(32)) bitadder_2 (.in0(B), .out(bitadder_2_out));
  Divider #(.width(32)) divider_1 (.a(A), .b(B), .out(divu8), .rem(remu9));  // open: upper
  Adder #(.width(6)) adder_1 (.a(bitadder_1_out), .b(bitadder_2_out), .out(adder_1_out));  // open: cin, cout
  assign cnto13 = {{26{1'b0}}, adder_1_out};  // Bit_Extender bit_extender_1
  Multiplier #(.width(32)) multiplier_1 (.a(A), .b(B), .out(mult10), .cout(mulhu11));  // open: cin
  Bit_Extender #(.in_width(32), .out_width(5)) bit_extender_2 (.in(B), .out(bit_extender_2_out));
  Bit_Extender #(.in_width(32), .out_width(5)) bit_extender_3 (.in(B), .out(bit_extender_3_out));
  Bit_Extender #(.in_width(32), .out_width(5)) bit_extender_4 (.in(B), .out(bit_extender_4_out));
  Comparator #(.width(32)) comparator_1 (.a(A), .b(B), .lt(comparator_1_lt));  // open: gt, eq
  Adder #(.width(32)) adder_2 (.a(A), .b(B), .out(add));  // open: cin, cout
  assign and1 = A & B;  // AND_Gate and_1, 32 bits wide
  assign or2 = A | B;  // OR_Gate or_1, 32 bits wide
  assign xor3 = A ^ B;  // XOR_Gate xor_1, 32 bits wide
  Shifter #(.width(32), .shift("lr")) shifter_1 (.in(A), .\dist (bit_extender_2_out), .out(srl4));
  Shifter #(.width(32), .shift("ar")) shifter_2 (.in(A), .\dist (bit_extender_3_out), .out(sra5));
  Shifter #(.width(32)) shifter_3 (.in(A), .\dist (bit_extender_4_out), .out(sll6));
  assign slt7 = {{31{1'b0}}, comparator_1_lt};  // Bit_Extender bit_extender_5
  Multiplexer #(.select(4), .width(32), .enable("false")) multiplexer_1 (
    .in0(add), .in1(and1), .in2(or2), .in3(xor3), .in4(srl4), .in5(sra5), .in6(sll6), .in7(slt7),
    .in8(divu8), .in9(remu9), .in10(mult10), .in11(mulhu11), .in12(sub12), .in13(cnto13), .in14(mulh14),
    .in15(B), .out(Result), .sel(ALUSel));
  Multiplier #(.width(32)) multiplier_2 (.a(abs_A), .b(abs_B), .out(abs_sl), .cout(abs_sh));  // open: cin
  Negator #(.width(32)) negator_1 (.in(B), .out(neg_B));
  Negator #(.width(32)) negator_2 (.in(abs_sl), .out(negator_2_out));
  Comparator #(.width(32), .mode("unsigned")) comparator_2 (
    .a(A), .b(32'h7fffffff), .gt(comparator_2_gt));  // open: eq, lt
  Comparator #(.width(32), .mode("unsigned")) comparator_3 (
    .a(B), .b(32'h7fffffff), .gt(comparator_3_gt));  // open: eq, lt
  Shifter #(.width(32), .shift("lr")) shifter_4 (.in(A), .\dist ({5{1'b1}}), .out(shifter_4_out));
  Shifter #(.width(32), .shift("lr")) shifter_5 (.in(B), .\dist ({5{1'b1}}), .out(shifter_5_out));
  Multiplexer #(.width(32), .enable("false")) multiplexer_2 (
    .in0(abs_sl), .in1(negator_2_out), .sel(sgn));  // open: out
  assign xor_2_out = shifter_4_out ^ shifter_5_out;  // XOR_Gate xor_2, 32 bits wide
  assign not_1_out = ~abs_sh;  // NOT_Gate not_1, 32 bits wide
  Negator #(.width(32)) negator_3 (.in(A), .out(neg_A));
  Multiplexer #(.width(32), .enable("false")) multiplexer_3 (.in0(A), .in1(neg_A), .out(abs_A), .sel(comparator_2_gt));
  Multiplexer #(.width(32), .enable("false")) multiplexer_4 (.in0(B), .in1(neg_B), .out(abs_B), .sel(comparator_3_gt));
  Bit_Extender #(.in_width(32), .out_width(1), .\type ("zero")) bit_extender_6 (.in(xor_2_out), .out(sgn));
  Multiplexer #(.width(32), .enable("false")) multiplexer_5 (
    .in0(abs_sh), .in1(not_1_out), .out(multiplexer_5_out), .sel(sgn));
  Adder #(.width(32)) adder_3 (.a(multiplexer_5_out), .b(undriven), .out(adder_3_out));  // open: cin, cout
  Comparator #(.width(32), .mode("unsigned")) comparator_4 (
    .a({32{1'b1}}), .b(abs_sl), .eq(comparator_4_eq));  // open: gt, lt
  Multiplexer #(.width(32), .enable("false")) multiplexer_6 (
    .in0(multiplexer_5_out), .in1(adder_3_out), .out(mulh14), .sel(comparator_4_eq));

  // Other names for the same wires on the sheet: lui15[31:0] = B

  // Notes on the sheet:
  //   INPUTS to your circuit
  //   DON'T CHANGE THE LOCATIONS OF THE INPUTS AND OUTPUTS!
  //   OUTPUT from your circuit
endmodule
