// Logisim project cpu.circ as structural Verilog: 5 circuits, main circuit main
module main (
  input  [31:0] INSTRUCTION,
  input  in_2,
  output [31:0] FETCH_ADDRESS,
  output [31:0] ra,
  output [31:0] sp,
  output [31:0] t0,
  output [31:0] t1,
  output [31:0] t2,
  output [31:0] s0,
  output [31:0] s1,
  output [31:0] a0
);

  wire ASel, BrEq, BrLT, BrUn, BSel, MemRW, PCSel, RegWEn;
  wire [1:0] Load, WBSel;
  wire [2:0] funct3, ImmSel;
  wire [3:0] ALUsel;
  wire [4:0] rd, rs1, rs2;
  wire [6:0] funct7, opcode;
  wire [31:0] adder_1_out, Arithmetic_Logic_Unit_result, bit_extender_1_out, bit_extender_2_out,
       DMEM_read_data, Imm, multiplexer_1_out, multiplexer_2_out, multiplexer_3_out, multiplexer_4_out,
       multiplexer_5_out, multiplexer_6_out, PC_q, RegFile_p7, RegFile_p8, register_2_q, register_3_q;

  ImmediateGenerator immediategenerator_1 (.in_2({funct7, rs2, rs1, funct3, rd, opcode}), .out_3(Imm), .in_1(ImmSel));
  Multiplexer #(.width(32), .enable("false")) multiplexer_1 (
    .in0(adder_1_out), .in1(Arithmetic_Logic_Unit_result), .out(multiplexer_1_out), .sel(PCSel));
  Register #(.width(32)) PC (.D(multiplexer_1_out), .clk(in_2), .Q(PC_q));  // open: en, clr
  Register #(.width(32)) register_1 (
    .D(multiplexer_2_out), .clk(in_2), .Q({funct7, rs2, rs1, funct3, rd, opcode}));  // open: en, clr
  Multiplexer #(.width(32), .enable("false")) multiplexer_2 (
    .in0(INSTRUCTION), .in1(32'h13), .out(multiplexer_2_out), .sel(PCSel));
  Adder #(.width(32)) adder_1 (.a(32'h4), .b(PC_q), .out(adder_1_out));  // open: cin, cout
  Shifter #(.width(32), .shift("ar")) shifter_1 (.in(PC_q), .\dist (5'b00010), .out(FETCH_ADDRESS));
  // Probe on opcode
  Register #(.width(32)) register_2 (.D(PC_q), .clk(in_2), .Q(register_2_q));  // open: en, clr
  // Probe on funct3
  Control control_1 (
    .in_1({funct7, rs2, rs1, funct3, rd, opcode}), ._1_ALU_2(WBSel), ._1_imm(ALUsel), ._0_Read(RegWEn),
    ._1_ALU(ImmSel), ._0_reg(BSel), ._1_Write(MemRW), .in_2(BrLT), .in_3(BrEq), .out_7(ASel), ._0__4(PCSel),
    .out_6(BrUn), ._2_PC_4(Load));
  // Probe on WBSel
  // Probe on rs2
  // Probe on rs1
  // Probe on rd
  // regfile_main RegFile: pin names not known; wires that end beside it: t0, t1, t2, s0, s1, a0, RegFile_p7, RegFile_p8
  Multiplexer #(.width(32), .enable("false")) multiplexer_3 (
    .in0(RegFile_p8), .in1(Imm), .out(multiplexer_3_out), .sel(BSel));
  Multiplexer #(.width(32), .enable("false")) multiplexer_4 (
    .in0(RegFile_p7), .in1(register_2_q), .out(multiplexer_4_out), .sel(ASel));
  branch_comp branch_comp_1 (.out_5(BrEq), .in_2(RegFile_p8), .in_3(BrUn), .in_1(RegFile_p7), .out_4(BrLT));
  // Probe on Arithmetic_Logic_Unit_result
  alu Arithmetic_Logic_Unit (
    .A(multiplexer_4_out), .B(multiplexer_3_out), .ALUSel(ALUsel), .Result(Arithmetic_Logic_Unit_result));
  Register #(.width(32)) register_3 (.D(adder_1_out), .clk(in_2), .Q(register_3_q));  // open: en, clr
  mem_main DMEM (
    .Address(Arithmetic_Logic_Unit_result), .Write_Data(RegFile_p8), .Write_En(MemRW),
    .Read_Data(DMEM_read_data), .clk(in_2));
  assign bit_extender_1_out = {{24{1'b0}}, DMEM_read_data[7:0]};  // Bit_Extender bit_extender_1
  assign bit_extender_2_out = {{16{1'b0}}, DMEM_read_data[15:0]};  // Bit_Extender bit_extender_2
  Multiplexer #(.select(2), .width(32), .enable("false")) multiplexer_5 (
    .in0(bit_extender_1_out), .in1(bit_extender_2_out), .in2(DMEM_read_data), .out(multiplexer_5_out),
    .sel(Load));  // open: in3
  Multiplexer #(.select(2), .width(32), .enable("false")) multiplexer_6 (
    .in0(multiplexer_5_out), .in1(Arithmetic_Logic_Unit_result), .in2(register_3_q), .out(multiplexer_6_out),
    .sel(WBSel));  // open: in3

  // Other names for the same wires on the sheet: clk = in_2; fetch_addr[31:0] = FETCH_ADDRESS

  // Notes on the sheet:
  //   Output
  //   Inputs/Outputs from run.circ. DO NOT MOVE THESE.
  //   Inputs
  //   It is OK to move the PC, RegFile, ALU, and MEM to wherever is most convenient for you when constructing your CPU, and to delete this text
  //   Inputs/Outputs from run.circ. DO NOT MOVE THESE.
endmodule

module test_addi (
  input  in_1,
  input  [31:0] in_2
);

  wire and_1_out, comparator_1_eq, comparator_2_eq, RegWEn, WBSel;
  wire [2:0] ImmSel;
  wire [3:0] ALUsel, main_1_p1;
  wire [31:0] alu_1_result, Imm, main_1_p3, main_2_read_data, multiplexer_2_out;

  // ImmediateGenerator immediategenerator_1: pin names not known; wires that end beside it: in_2[31:20], Imm
  // Control control_1: pin names not known; wires that end beside it: in_2[6:0], in_2[14:12], ALUsel, WBSel, RegWEn, ImmSel
  Comparator #(.width(7)) comparator_1 (.a(in_2[6:0]), .b(7'b0010011), .eq(comparator_1_eq));  // open: gt, lt
  Comparator #(.width(3)) comparator_2 (.a(in_2[14:12]), .b(3'b000), .eq(comparator_2_eq));  // open: gt, lt
  and and_1 (and_1_out, comparator_1_eq, comparator_2_eq);
  // regfile_main main_1: pin names not known; wires that end beside it: main_1_p1, ALUsel, main_1_p3
  Multiplexer #(.width(4), .enable("false")) multiplexer_1 (
    .in0(4'b1110), .in1(4'b0000), .out(main_1_p1), .sel(and_1_out));
  alu alu_1 (.A(main_1_p3), .B(Imm), .ALUSel(ALUsel), .Result(alu_1_result));
  mem_main main_2 (.Address(alu_1_result), .Read_Data(main_2_read_data));  // open: Write_Data, Write_En, clk
  Multiplexer #(.width(32), .enable("false")) multiplexer_2 (
    .in0(main_2_read_data), .in1(alu_1_result), .out(multiplexer_2_out), .sel(WBSel));

  // Other names for the same wires on the sheet: clk = in_1; INSTRUCTION[31:0] = in_2; opcode[6:0] = in_2[6:0];
  //   rd[4:0] = in_2[11:7]; funct3[2:0] = in_2[14:12]; rs1[4:0] = in_2[19:15]; ImmI[11:0] = in_2[31:20]

  // Notes on the sheet:
  //   啊可能在control里处理了
  //   需要判断instype，imm的种类
  //   这个没啥用比较粗糙的control，只用来add
endmodule

module ImmediateGenerator (
  input  [2:0] in_1,
  input  [31:0] in_2,
  output [31:0] out_3
);

  wire [31:11] i, s;
  wire [31:12] b;
  wire [31:20] j;

  assign i = {{20{in_2[31]}}, in_2[31]};  // Bit_Extender bit_extender_1
  assign s = {{20{in_2[31]}}, in_2[31]};  // Bit_Extender bit_extender_2
  assign b = {{19{in_2[31]}}, in_2[31]};  // Bit_Extender bit_extender_3
  assign j = {{11{in_2[31]}}, in_2[31]};  // Bit_Extender bit_extender_4
  Multiplexer #(.select(3), .width(32), .enable("false")) multiplexer_1 (
    .in0({i, in_2[30:20]}), .in1({s, in_2[30:25], in_2[11:7]}),
    .in2({b, in_2[7], in_2[30:25], in_2[11:8], 1'b0}), .in3({in_2[31:12], {12{1'b0}}}),
    .in4({j, in_2[19:12], in_2[20], in_2[30:21], 1'b0}), .out(out_3), .sel(in_1));  // open: in5, in6, in7

  // Other names for the same wires on the sheet: b[11:1] = {in_2[7], in_2[30:25], in_2[11:8]}; inst[31:0] = in_2;
  //   s[10:0] = {in_2[30:25], in_2[11:7]}; Imm[31:0] = out_3; ImmSel[2:0] = in_1; i[10:0] = in_2[30:20];
  //   j[19:1] = {in_2[19:12], in_2[20], in_2[30:21]}; u[31:12] = in_2[31:12]
endmodule

module Control (
  input  [31:0] in_1,
  input  in_2,
  input  in_3,
  output _0__4,
  output [2:0] _1_ALU,
  output out_6,
  output out_7,
  output _0_reg,
  output [3:0] _1_imm,
  output _1_Write,
  output _0_Read,
  output [1:0] _1_ALU_2,
  output [1:0] _2_PC_4
);

  wire and_28_out, and_29_out, and_30_out, and_31_out, btype, is_add, is_addi, is_and, is_andi, is_beq,
       is_blt, is_bltu, is_bne, is_divu, is_jal, is_jalr, is_lb, is_lh, is_lui, is_lw, is_mul, is_mulh,
       is_mulhu, is_or, is_ori, is_remu, is_sll, is_slli, is_slt, is_slti, is_srai, is_srl, is_srli, is_sub,
       is_xor, is_xori, itype, not_1_out, not_2_out, not_3_out, not_4_out, not_5_out, not_6_out, not_7_out,
       not_8_out, not_9_out, not_10_out, not_11_out, not_12_out, not_13_out, not_14_out, not_15_out,
       not_16_out, not_17_out, not_18_out, not_19_out, not_20_out, not_21_out, not_22_out, not_23_out,
       not_24_out, not_25_out, not_26_out, not_27_out, not_28_out, not_29_out, not_30_out, not_31_out,
       not_32_out, not_33_out, not_34_out, not_35_out, not_36_out, not_37_out, not_38_out, not_39_out,
       not_40_out, not_41_out, not_42_out, not_43_out, not_44_out, not_45_out, not_46_out, not_47_out,
       not_48_out, not_49_out, not_50_out, not_51_out, not_52_out, not_53_out, not_54_out, not_55_out,
       not_56_out, not_57_out, not_58_out, not_59_out, not_60_out, not_61_out, not_62_out, not_63_out,
       not_64_out, not_65_out, not_66_out, not_67_out, not_68_out, not_69_out, not_70_out, not_71_out,
       not_72_out, not_73_out, not_74_out, not_75_out, not_76_out, not_77_out, not_78_out, not_79_out,
       not_80_out, not_81_out, not_82_out, not_83_out, not_84_out, not_85_out, not_86_out, not_87_out,
       not_88_out, not_89_out, not_90_out, not_91_out, not_92_out, not_93_out, not_94_out, not_95_out,
       not_96_out, not_97_out, not_98_out, not_99_out, not_100_out, not_101_out, not_102_out, not_103_out,
       not_104_out, not_105_out, not_106_out, not_107_out, not_108_out, not_109_out, not_110_out,
       not_111_out, not_112_out, not_113_out, not_114_out, not_115_out, not_116_out, not_117_out,
       not_118_out, not_119_out, not_120_out, not_121_out, not_122_out, not_123_out, not_124_out,
       not_125_out, not_126_out, not_127_out, not_128_out, not_129_out, not_130_out, not_131_out,
       not_132_out, not_133_out, not_134_out, not_135_out, not_136_out, not_137_out, not_138_out,
       not_139_out, not_140_out, not_141_out, not_142_out, not_143_out, not_144_out, not_145_out,
       not_146_out, not_147_out, not_148_out, not_149_out, not_150_out, not_151_out, not_152_out,
       not_153_out, not_154_out, not_155_out, not_156_out, not_157_out, not_158_out, not_159_out,
       not_160_out, not_161_out, not_162_out, not_163_out, not_164_out, not_165_out, not_166_out,
       not_167_out, not_168_out, not_169_out, not_170_out, not_171_out, not_172_out, not_173_out,
       not_174_out, not_175_out, not_176_out, not_177_out, not_178_out, not_179_out, not_180_out,
       not_181_out, not_182_out, not_183_out, not_184_out, not_185_out, not_186_out, not_187_out,
       not_188_out, not_189_out, not_190_out, not_191_out, not_192_out, or_3_out, or_4_out, or_6_out,
       or_7_out, or_8_out, or_9_out, or_10_out, or_12_out, or_13_out, or_14_out, or_15_out, rtype;
  wire [1:0] multiplexer_1_out, multiplexer_4_out, multiplexer_20_out, multiplexer_21_out;
  wire [2:0] multiplexer_6_out, multiplexer_9_out, multiplexer_13_out;
  wire [3:0] multiplexer_3_out, multiplexer_5_out, multiplexer_7_out, multiplexer_8_out, multiplexer_11_out,
       multiplexer_12_out, multiplexer_14_out, multiplexer_15_out, multiplexer_17_out, multiplexer_18_out,
       multiplexer_19_out, multiplexer_22_out, multiplexer_23_out, multiplexer_25_out;

  // Probe on in_1
  not not_1 (not_1_out, in_1[2]);
  not not_2 (not_2_out, in_1[3]);
  not not_3 (not_3_out, in_1[6]);
  not not_4 (not_4_out, in_1[30]);
  not not_5 (not_5_out, in_1[2]);
  not not_6 (not_6_out, in_1[3]);
  not not_7 (not_7_out, in_1[5]);
  not not_8 (not_8_out, in_1[6]);
  not not_9 (not_9_out, in_1[13]);
  not not_10 (not_10_out, in_1[14]);
  not not_11 (not_11_out, in_1[25]);
  not not_12 (not_12_out, in_1[30]);
  not not_13 (not_13_out, in_1[2]);
  not not_14 (not_14_out, in_1[3]);
  not not_15 (not_15_out, in_1[5]);
  not not_16 (not_16_out, in_1[6]);
  not not_17 (not_17_out, in_1[12]);
  and and_1 (is_ori, not_13_out, not_14_out, in_1[4], not_15_out, not_16_out, not_17_out, in_1[13], in_1[14], 1'b1, 1'b1);
  and and_2 (is_remu, not_1_out, not_2_out, in_1[4], in_1[5], not_3_out, in_1[12], in_1[13], in_1[14], in_1[25], not_4_out);
  and and_3 (is_slli, not_5_out, not_6_out, in_1[4], not_7_out, not_8_out, in_1[12], not_9_out, not_10_out, not_11_out, not_12_out);
  not not_18 (not_18_out, in_1[2]);
  not not_19 (not_19_out, in_1[3]);
  not not_20 (not_20_out, in_1[6]);
  not not_21 (not_21_out, in_1[12]);
  not not_22 (not_22_out, in_1[13]);
  not not_23 (not_23_out, in_1[14]);
  not not_24 (not_24_out, in_1[25]);
  not not_25 (not_25_out, in_1[30]);
  not not_26 (not_26_out, in_1[2]);
  not not_27 (not_27_out, in_1[3]);
  not not_28 (not_28_out, in_1[6]);
  not not_29 (not_29_out, in_1[12]);
  not not_30 (not_30_out, in_1[13]);
  not not_31 (not_31_out, in_1[14]);
  not not_32 (not_32_out, in_1[25]);
  not not_33 (not_33_out, in_1[2]);
  not not_34 (not_34_out, in_1[3]);
  not not_35 (not_35_out, in_1[6]);
  not not_36 (not_36_out, in_1[12]);
  not not_37 (not_37_out, in_1[13]);
  not not_38 (not_38_out, in_1[25]);
  not not_39 (not_39_out, in_1[30]);
  not not_40 (not_40_out, in_1[2]);
  not not_41 (not_41_out, in_1[3]);
  not not_42 (not_42_out, in_1[6]);
  not not_43 (not_43_out, in_1[12]);
  not not_44 (not_44_out, in_1[25]);
  not not_45 (not_45_out, in_1[30]);
  not not_46 (not_46_out, in_1[2]);
  not not_47 (not_47_out, in_1[3]);
  not not_48 (not_48_out, in_1[5]);
  not not_49 (not_49_out, in_1[6]);
  not not_50 (not_50_out, in_1[12]);
  not not_51 (not_51_out, in_1[14]);
  not not_52 (not_52_out, in_1[2]);
  not not_53 (not_53_out, in_1[3]);
  not not_54 (not_54_out, in_1[5]);
  not not_55 (not_55_out, in_1[6]);
  and and_4 (is_add, not_18_out, not_19_out, in_1[4], in_1[5], not_20_out, not_21_out, not_22_out, not_23_out, not_24_out, not_25_out);
  and and_5 (is_sub, not_26_out, not_27_out, in_1[4], in_1[5], not_28_out, not_29_out, not_30_out, not_31_out, not_32_out, in_1[30]);
  and and_6 (is_xor, not_33_out, not_34_out, in_1[4], in_1[5], not_35_out, not_36_out, not_37_out, in_1[14], not_38_out, not_39_out);
  and and_7 (is_or, not_40_out, not_41_out, in_1[4], in_1[5], not_42_out, not_43_out, in_1[13], in_1[14], not_44_out, not_45_out);
  and and_8 (is_slti, not_46_out, not_47_out, in_1[4], not_48_out, not_49_out, not_50_out, in_1[13], not_51_out, 1'b1, 1'b1);
  and and_9 (is_andi, not_52_out, not_53_out, in_1[4], not_54_out, not_55_out, in_1[12], in_1[13], in_1[14], 1'b1, 1'b1);
  not not_56 (not_56_out, in_1[2]);
  not not_57 (not_57_out, in_1[3]);
  not not_58 (not_58_out, in_1[6]);
  not not_59 (not_59_out, in_1[12]);
  not not_60 (not_60_out, in_1[14]);
  not not_61 (not_61_out, in_1[25]);
  not not_62 (not_62_out, in_1[30]);
  not not_63 (not_63_out, in_1[2]);
  not not_64 (not_64_out, in_1[3]);
  not not_65 (not_65_out, in_1[6]);
  not not_66 (not_66_out, in_1[13]);
  not not_67 (not_67_out, in_1[14]);
  not not_68 (not_68_out, in_1[25]);
  not not_69 (not_69_out, in_1[30]);
  not not_70 (not_70_out, in_1[2]);
  not not_71 (not_71_out, in_1[3]);
  not not_72 (not_72_out, in_1[6]);
  not not_73 (not_73_out, in_1[13]);
  not not_74 (not_74_out, in_1[25]);
  not not_75 (not_75_out, in_1[30]);
  not not_76 (not_76_out, in_1[2]);
  not not_77 (not_77_out, in_1[3]);
  not not_78 (not_78_out, in_1[6]);
  not not_79 (not_79_out, in_1[25]);
  not not_80 (not_80_out, in_1[30]);
  not not_81 (not_81_out, in_1[2]);
  not not_82 (not_82_out, in_1[3]);
  not not_83 (not_83_out, in_1[5]);
  not not_84 (not_84_out, in_1[6]);
  not not_85 (not_85_out, in_1[12]);
  not not_86 (not_86_out, in_1[13]);
  not not_87 (not_87_out, in_1[2]);
  not not_88 (not_88_out, in_1[3]);
  not not_89 (not_89_out, in_1[4]);
  not not_90 (not_90_out, in_1[6]);
  not not_91 (not_91_out, in_1[12]);
  not not_92 (not_92_out, in_1[14]);
  and and_10 (is_slt, not_56_out, not_57_out, in_1[4], in_1[5], not_58_out, not_59_out, in_1[13], not_60_out, not_61_out, not_62_out);
  and and_11 (is_sll, not_63_out, not_64_out, in_1[4], in_1[5], not_65_out, in_1[12], not_66_out, not_67_out, not_68_out, not_69_out);
  and and_12 (is_srl, not_70_out, not_71_out, in_1[4], in_1[5], not_72_out, in_1[12], not_73_out, in_1[14], not_74_out, not_75_out);
  and and_13 (is_and, not_76_out, not_77_out, in_1[4], in_1[5], not_78_out, in_1[12], in_1[13], in_1[14], not_79_out, not_80_out);
  and and_14 (is_xori, not_81_out, not_82_out, in_1[4], not_83_out, not_84_out, not_85_out, not_86_out, in_1[14], 1'b1, 1'b1);
  and and_15 (_1_Write, not_87_out, not_88_out, not_89_out, in_1[5], not_90_out, not_91_out, in_1[13], not_92_out, 1'b1, 1'b1);
  not not_93 (not_93_out, in_1[2]);
  not not_94 (not_94_out, in_1[3]);
  not not_95 (not_95_out, in_1[6]);
  not not_96 (not_96_out, in_1[12]);
  not not_97 (not_97_out, in_1[13]);
  not not_98 (not_98_out, in_1[14]);
  not not_99 (not_99_out, in_1[30]);
  not not_100 (not_100_out, in_1[2]);
  not not_101 (not_101_out, in_1[3]);
  not not_102 (not_102_out, in_1[6]);
  not not_103 (not_103_out, in_1[13]);
  not not_104 (not_104_out, in_1[14]);
  not not_105 (not_105_out, in_1[30]);
  not not_106 (not_106_out, in_1[2]);
  not not_107 (not_107_out, in_1[3]);
  not not_108 (not_108_out, in_1[6]);
  not not_109 (not_109_out, in_1[14]);
  not not_110 (not_110_out, in_1[30]);
  not not_111 (not_111_out, in_1[2]);
  not not_112 (not_112_out, in_1[3]);
  not not_113 (not_113_out, in_1[6]);
  not not_114 (not_114_out, in_1[13]);
  not not_115 (not_115_out, in_1[30]);
  not not_116 (not_116_out, in_1[2]);
  not not_117 (not_117_out, in_1[3]);
  not not_118 (not_118_out, in_1[5]);
  not not_119 (not_119_out, in_1[6]);
  not not_120 (not_120_out, in_1[13]);
  not not_121 (not_121_out, in_1[25]);
  not not_122 (not_122_out, in_1[30]);
  not not_123 (not_123_out, in_1[2]);
  not not_124 (not_124_out, in_1[3]);
  not not_125 (not_125_out, in_1[4]);
  not not_126 (not_126_out, in_1[12]);
  not not_127 (not_127_out, in_1[13]);
  not not_128 (not_128_out, in_1[14]);
  and and_16 (is_mul, not_93_out, not_94_out, in_1[4], in_1[5], not_95_out, not_96_out, not_97_out, not_98_out, in_1[25], not_99_out);
  and and_17 (is_mulh, not_100_out, not_101_out, in_1[4], in_1[5], not_102_out, in_1[12], not_103_out, not_104_out, in_1[25], not_105_out);
  and and_18 (is_mulhu, not_106_out, not_107_out, in_1[4], in_1[5], not_108_out, in_1[12], in_1[13], not_109_out, in_1[25], not_110_out);
  and and_19 (is_divu, not_111_out, not_112_out, in_1[4], in_1[5], not_113_out, in_1[12], not_114_out, in_1[14], in_1[25], not_115_out);
  and and_20 (is_srli, not_116_out, not_117_out, in_1[4], not_118_out, not_119_out, in_1[12], not_120_out, in_1[14], not_121_out, not_122_out);
  and and_21 (is_beq, not_123_out, not_124_out, not_125_out, in_1[5], in_1[6], not_126_out, not_127_out, not_128_out, 1'b1, 1'b1);
  not not_129 (not_129_out, in_1[2]);
  not not_130 (not_130_out, in_1[3]);
  not not_131 (not_131_out, in_1[4]);
  not not_132 (not_132_out, in_1[5]);
  not not_133 (not_133_out, in_1[6]);
  not not_134 (not_134_out, in_1[12]);
  not not_135 (not_135_out, in_1[13]);
  not not_136 (not_136_out, in_1[14]);
  not not_137 (not_137_out, in_1[2]);
  not not_138 (not_138_out, in_1[3]);
  not not_139 (not_139_out, in_1[4]);
  not not_140 (not_140_out, in_1[5]);
  not not_141 (not_141_out, in_1[6]);
  not not_142 (not_142_out, in_1[13]);
  not not_143 (not_143_out, in_1[14]);
  not not_144 (not_144_out, in_1[2]);
  not not_145 (not_145_out, in_1[3]);
  not not_146 (not_146_out, in_1[4]);
  not not_147 (not_147_out, in_1[5]);
  not not_148 (not_148_out, in_1[6]);
  not not_149 (not_149_out, in_1[12]);
  not not_150 (not_150_out, in_1[14]);
  not not_151 (not_151_out, in_1[2]);
  not not_152 (not_152_out, in_1[3]);
  not not_153 (not_153_out, in_1[5]);
  not not_154 (not_154_out, in_1[6]);
  not not_155 (not_155_out, in_1[12]);
  not not_156 (not_156_out, in_1[13]);
  not not_157 (not_157_out, in_1[14]);
  not not_158 (not_158_out, in_1[2]);
  not not_159 (not_159_out, in_1[3]);
  not not_160 (not_160_out, in_1[5]);
  not not_161 (not_161_out, in_1[6]);
  not not_162 (not_162_out, in_1[13]);
  not not_163 (not_163_out, in_1[25]);
  not not_164 (not_164_out, in_1[2]);
  not not_165 (not_165_out, in_1[3]);
  not not_166 (not_166_out, in_1[4]);
  not not_167 (not_167_out, in_1[13]);
  not not_168 (not_168_out, in_1[14]);
  and and_22 (is_lb, not_129_out, not_130_out, not_131_out, not_132_out, not_133_out, not_134_out, not_135_out, not_136_out, 1'b1, 1'b1);
  and and_23 (is_lh, not_137_out, not_138_out, not_139_out, not_140_out, not_141_out, in_1[12], not_142_out, not_143_out, 1'b1, 1'b1);
  and and_24 (is_lw, not_144_out, not_145_out, not_146_out, not_147_out, not_148_out, not_149_out, in_1[13], not_150_out, 1'b1, 1'b1);
  and and_25 (is_addi, not_151_out, not_152_out, in_1[4], not_153_out, not_154_out, not_155_out, not_156_out, not_157_out, 1'b1, 1'b1);
  and and_26 (is_srai, not_158_out, not_159_out, in_1[4], not_160_out, not_161_out, in_1[12], not_162_out, in_1[14], not_163_out, in_1[30]);
  and and_27 (is_bne, not_164_out, not_165_out, not_166_out, in_1[5], in_1[6], in_1[12], not_167_out, not_168_out, 1'b1, 1'b1);
  not not_169 (not_169_out, in_3);
  and and_28 (and_28_out, is_beq, in_3);
  and and_29 (and_29_out, is_bne, not_169_out);
  not not_170 (not_170_out, is_blt);
  not not_171 (not_171_out, in_1[3]);
  not not_172 (not_172_out, in_1[6]);
  not not_173 (not_173_out, in_1[2]);
  not not_174 (not_174_out, in_1[3]);
  not not_175 (not_175_out, in_1[4]);
  not not_176 (not_176_out, in_1[12]);
  not not_177 (not_177_out, in_1[13]);
  and and_30 (and_30_out, is_blt, in_2);
  and and_31 (and_31_out, is_bltu, in_2);
  not not_178 (not_178_out, in_1[3]);
  not not_179 (not_179_out, in_1[4]);
  not not_180 (not_180_out, in_1[12]);
  not not_181 (not_181_out, in_1[13]);
  not not_182 (not_182_out, in_1[14]);
  or or_1 (out_6, is_bltu, not_170_out);
  and and_32 (is_jalr, in_1[2], not_178_out, not_179_out, in_1[5], in_1[6], not_180_out, not_181_out, not_182_out, 1'b1, 1'b1);
  and and_33 (is_lui, in_1[2], not_171_out, in_1[4], in_1[5], not_172_out, 1'b1, 1'b1, 1'b1, 1'b1, 1'b1);
  and and_34 (is_blt, not_173_out, not_174_out, not_175_out, in_1[5], in_1[6], not_176_out, not_177_out, in_1[14], 1'b1, 1'b1);
  or or_2 (_0__4, is_jalr, is_jal, and_28_out, and_29_out, and_30_out, and_31_out);
  not not_183 (not_183_out, in_1[4]);
  not not_184 (not_184_out, in_1[2]);
  not not_185 (not_185_out, in_1[3]);
  not not_186 (not_186_out, in_1[4]);
  not not_187 (not_187_out, in_1[12]);
  and and_35 (is_jal, in_1[2], in_1[3], not_183_out, in_1[5], in_1[6], 1'b1, 1'b1, 1'b1, 1'b1, 1'b1);
  and and_36 (is_bltu, not_184_out, not_185_out, not_186_out, in_1[5], in_1[6], not_187_out, in_1[13], in_1[14], 1'b1, 1'b1);
  not not_188 (not_188_out, is_bne);
  not not_189 (not_189_out, is_beq);
  not not_190 (not_190_out, is_bltu);
  not not_191 (not_191_out, is_blt);
  not not_192 (not_192_out, _1_Write);
  or or_3 (or_3_out, is_add, is_sub, is_mul, is_divu, is_sll, is_mulh, is_mulhu, is_srl, is_slt, is_remu, is_or, is_and, is_xor);
  Multiplexer #(.width(2), .enable("false")) multiplexer_1 (
    .in1(2'b01), .out(multiplexer_1_out), .sel(or_4_out));  // open: in0
  or or_4 (or_4_out, rtype, is_lui, itype);
  Multiplexer #(.width(4), .enable("false")) multiplexer_2 (
    .in0(multiplexer_3_out), .in1(4'b1111), .out(_1_imm), .sel(is_lui));
  or or_5 (out_7, is_bne, is_beq, is_bltu, is_blt, is_jal);
  and and_37 (_0_Read, not_188_out, not_189_out, not_190_out, not_191_out, not_192_out);
  not not_193 (_0_reg, or_3_out);
  or or_6 (or_6_out, is_jalr, is_jal);
  Multiplexer #(.width(4), .enable("false")) multiplexer_3 (
    .in0(multiplexer_5_out), .in1(4'b1110), .out(multiplexer_3_out), .sel(is_mulh));
  Multiplexer #(.width(2), .enable("false")) multiplexer_4 (
    .in0(multiplexer_1_out), .in1(2'b10), .out(multiplexer_4_out), .sel(or_6_out));
  or or_7 (or_7_out, _1_Write, is_lb, is_lh, is_lw, is_jal, is_add, is_bne, is_beq, is_bltu, is_blt, is_jalr, is_addi);
  Multiplexer #(.width(4), .enable("false")) multiplexer_5 (
    .in0(multiplexer_8_out), .in1(4'b1100), .out(multiplexer_5_out), .sel(is_sub));
  Multiplexer #(.width(3), .enable("false")) multiplexer_6 (
    .in0(3'b000), .in1(3'b001), .out(multiplexer_6_out), .sel(_1_Write));
  or or_8 (or_8_out, is_lw, is_lh, is_lb);
  Multiplexer #(.width(4), .enable("false")) multiplexer_7 (
    .in1(4'b0000), .out(multiplexer_7_out), .sel(or_7_out));  // open: in0
  or or_9 (or_9_out, is_srl, is_srli);
  Multiplexer #(.width(4), .enable("false")) multiplexer_8 (
    .in0(multiplexer_12_out), .in1(4'b1011), .out(multiplexer_8_out), .sel(is_mulhu));
  Multiplexer #(.width(3), .enable("false")) multiplexer_9 (
    .in0(multiplexer_6_out), .in1(3'b010), .out(multiplexer_9_out), .sel(btype));
  Multiplexer #(.width(2), .enable("false")) multiplexer_10 (
    .in0(multiplexer_4_out), .in1(2'b00), .out(_1_ALU_2), .sel(or_8_out));
  Multiplexer #(.width(4), .enable("false")) multiplexer_11 (
    .in0(multiplexer_7_out), .in1(4'b0001), .out(multiplexer_11_out), .sel(or_10_out));
  or or_10 (or_10_out, is_and, is_andi);
  Multiplexer #(.width(4), .enable("false")) multiplexer_12 (
    .in0(multiplexer_15_out), .in1(4'b1001), .out(multiplexer_12_out), .sel(is_remu));
  or or_11 (rtype, is_add, is_sub, is_mul, is_divu, is_sll, is_mulh, is_mulhu, is_srl, is_slt, is_remu, is_or, is_and, is_xor);
  Multiplexer #(.width(3), .enable("false")) multiplexer_13 (
    .in0(multiplexer_9_out), .in1(3'b011), .out(multiplexer_13_out), .sel(is_lui));
  Multiplexer #(.width(4), .enable("false")) multiplexer_14 (
    .in0(multiplexer_11_out), .in1(4'b0010), .out(multiplexer_14_out), .sel(or_12_out));
  or or_12 (or_12_out, is_or, is_ori);
  or or_13 (or_13_out, is_xor, is_xori);
  Multiplexer #(.width(4), .enable("false")) multiplexer_15 (
    .in0(multiplexer_19_out), .in1(4'b1000), .out(multiplexer_15_out), .sel(is_divu));
  or or_14 (or_14_out, is_slti, is_slt);
  Multiplexer #(.width(3), .enable("false")) multiplexer_16 (
    .in0(multiplexer_13_out), .in1(3'b100), .out(_1_ALU), .sel(is_jal));
  Multiplexer #(.width(4), .enable("false")) multiplexer_17 (
    .in0(multiplexer_14_out), .in1(4'b0011), .out(multiplexer_17_out), .sel(or_13_out));
  Multiplexer #(.width(4), .enable("false")) multiplexer_18 (
    .in0(multiplexer_17_out), .in1(4'b0100), .out(multiplexer_18_out), .sel(or_9_out));
  or or_15 (or_15_out, is_sll, is_slli);
  Multiplexer #(.width(4), .enable("false")) multiplexer_19 (
    .in0(multiplexer_23_out), .in1(4'b0111), .out(multiplexer_19_out), .sel(or_14_out));
  Multiplexer #(.width(2), .enable("false")) multiplexer_20 (
    .in1(2'b00), .out(multiplexer_20_out), .sel(is_lb));  // open: in0
  Multiplexer #(.width(2), .enable("false")) multiplexer_21 (
    .in0(multiplexer_20_out), .in1(2'b01), .out(multiplexer_21_out), .sel(is_lh));
  Multiplexer #(.width(4), .enable("false")) multiplexer_22 (
    .in0(multiplexer_18_out), .in1(4'b0110), .out(multiplexer_22_out), .sel(or_15_out));
  Multiplexer #(.width(4), .enable("false")) multiplexer_23 (
    .in0(multiplexer_25_out), .in1(4'b1010), .out(multiplexer_23_out), .sel(is_mul));
  or or_16 (btype, is_bne, is_beq, is_bltu, is_blt);
  Multiplexer #(.width(2), .enable("false")) multiplexer_24 (
    .in0(multiplexer_21_out), .in1(2'b10), .out(_2_PC_4), .sel(is_lw));
  Multiplexer #(.width(4), .enable("false")) multiplexer_25 (
    .in0(multiplexer_22_out), .in1(4'b0101), .out(multiplexer_25_out), .sel(is_srai));
  or or_17 (itype, is_jalr, is_addi, is_lw, is_srai, is_slli, is_lh, is_srli, is_slti, is_xori, is_ori, is_andi, is_lb);

  // Other names for the same wires on the sheet: ALUsel[3:0] = _1_imm; ASel = out_7; BrEq = in_3; BrLT = in_2;
  //   BrUn = out_6; BSel = _0_reg; ImmSel[2:0] = _1_ALU; Inst[31:0] = in_1; d_2 = in_1[2]; d_3 = in_1[3];
  //   d_4 = in_1[4]; d_5 = in_1[5]; d_6 = in_1[6]; d_12 = in_1[12]; d_13 = in_1[13]; d_14 = in_1[14]; d_25 = in_1[25];
  //   d_30 = in_1[30]; jtype = is_jal; LoadSel[1:0] = _2_PC_4; PCSel = _0__4; RegWEn = _0_Read; is_sw = _1_Write;
  //   MemRW = _1_Write; stype = _1_Write; utype = is_lui; WBSel[1:0] = _1_ALU_2

  // Notes on the sheet:
  //   掐指一算是第25位
  //   5/7：R画完啦
  //   我开始考虑一层层匹配了
  //   虽然多拿一位就可以解决了
  //   0 Mem
  //   CA欺我，mulh什么的不止需要9个bit，他们的funct7是0x01
  //   jal是1，sw是0
endmodule

module branch_comp (
  input  [31:0] in_1,
  input  [31:0] in_2,
  input  in_3,
  output out_4,
  output out_5
);

  wire comparator_1_lt, comparator_2_lt;

  Comparator #(.width(32)) comparator_1 (.a(in_1), .b(in_2), .eq(out_5), .lt(comparator_1_lt));  // open: gt
  Comparator #(.width(32), .mode("unsigned")) comparator_2 (.a(in_1), .b(in_2), .lt(comparator_2_lt));  // open: gt, eq
  Multiplexer #(.enable("false")) multiplexer_1 (.in0(comparator_1_lt), .in1(comparator_2_lt), .out(out_4), .sel(in_3));

  // Other names for the same wires on the sheet: a[31:0] = in_1; b[31:0] = in_2; breq = out_5; brlt = out_4;
  //   brun = in_3
endmodule
